# Fritzing sketch robotline (saved by Fritzing 0.8.7b)
circuit board: 7.5cm x 5cm
breadboards: 1

parts:
  XTAL1 = Crystal [frequency="16 MHz" package=THT]
  C1 = Ceramic Capacitor [capacitance=22pF package="200 mil [THT, multilayer]"]
  C2 = Ceramic Capacitor [capacitance=22pF package="200 mil [THT, multilayer]"]
  U1 = Voltage Regulator - 5V [package="TO220 [THT]"]
  C3 = Electrolytic Capacitor [capacitance=10µF voltage=10V package="100 mil [THT, electrolytic]"]
  C4 = Electrolytic Capacitor [capacitance=10µF voltage=10V package="100 mil [THT, electrolytic]"]
  LED1 = LED - 5mm [color="Red (633nm)" package="5 mm [THT]"]
  R1 = Resistor [tolerance=±5% resistance=1k package=THT]
  R2 = Resistor [tolerance=±5% resistance=10k package=THT]
  LED2 = LED - 5mm [color="Red (633nm)" package="5 mm [THT]"]
  R3 = Resistor [tolerance=±5% resistance=1k package=THT]
  C5 = Ceramic Capacitor [capacitance=10nF package="100 mil [THT, multilayer]"]
  serie = female pin header, 4 pins [form="♀ (female)"]
  Mot_De = Basic Servo
  ServoI = Basic Servo
  LEDD = LED - 5mm [color="Red (633nm)" package="5 mm [THT]"]
  LEDI = LED - 5mm [color="Red (633nm)" package="5 mm [THT]"]
  R4 = Resistor [tolerance=±5% resistance=1k package=THT]
  R5 = Resistor [tolerance=±5% resistance=1k package=THT]
  R6 = Resistor [tolerance=±5% resistance=10k package=THT]
  S2 = Momentary Switch [package=tactile-pth]
  Arduino = atmega328 [package=dip]
  J2 = female pin header, 3 pins [form="♀ (female)"]
  J3 = female pin header, 1 pin [form="♀ (female)"]
  INPUT = female pin header, 2 pins [form="♀ (female)"]
  LineD = female pin header, 3 pins [form="♀ (female)"]
  LineaI = female pin header, 3 pins [form="♀ (female)"]
  J1 = female pin header, 4 pins [form="♀ (female)"]

nets:
  N1: XTAL1.pin_0, C2.1, Arduino.XLAT2
  N2: XTAL1.pin_1, C1.1, Arduino.XLAT1
  GND: C1.0, C2.0, U1.GND, C3.-, C4.-, LED1.cathode, LED2.cathode, serie.pin4, Mot_De.gnd, ServoI.gnd, LEDD.cathode, LEDI.cathode, R6.Pin_1, Arduino.GND, INPUT.pin2, LineD.pin2, LineaI.pin2
  9V: U1.input_voltage, C3.+, INPUT.pin1
  5V: U1.output_voltage, C4.+, R1.Pin_0, R2.Pin_0, Mot_De.vcc, ServoI.vcc, S2.1, Arduino.VCC, Arduino.AVCC
  N3: LED1.anode, R1.Pin_1
  N4: R2.Pin_1, C5.1, Arduino.RESET
  N5: LED2.anode, R3.Pin_1
  N6: R3.Pin_0, Arduino.D13
  N7: C5.0, serie.pin1
  N8: serie.pin2, Arduino.D0_(RX)
  N9: serie.pin3, Arduino.D1_(TX)
  Motor_Derecho: Mot_De.pulse, Arduino.D2
  Motor_Izquierdo: ServoI.pulse, Arduino.D3_(PWM)
  N10: LEDD.anode, R4.Pin_1
  N11: LEDI.anode, R5.Pin_1
  LedD: R4.Pin_0, Arduino.D5_(PWM)
  LedI: R5.Pin_0, Arduino.D6_(PWM)
  N12: R6.Pin_0, S2.4
  sw: S2.3, Arduino.D4
  N13: Arduino.D7, J3.pin1
  liena2: Arduino.D8, LineaI.pin1
  linea1: Arduino.D9_(PWM), LineD.pin1
  N14: Arduino.D10_(PWM), J2.pin3
  N15: Arduino.D11_(PWM), J2.pin2
  N16: Arduino.D12, J2.pin1
  A0: Arduino.A0, LineD.pin3
  A1: Arduino.A1, LineaI.pin3
  N17: Arduino.A2, J1.pin4
  N18: Arduino.A3, J1.pin3
  N19: Arduino.A4, J1.pin2
  N20: Arduino.A5, J1.pin1
